# Fritzing sketch anemio_v1 (saved by Fritzing 0.9.3b)

parts:
  Pressure = Adafruit_BMP280
  Ambient_Light = Ambient Light Sensor (TEMT6000 Breakout Board)
  DHT1 = DHT22 Humidity and Temperature Sensor
  J$1 = SMA Antenna Connector [package=sma-edge]
  Compass_+_Accelerometer = Adafruit LSM303DLHC Triple-axis Accelerometer+Magnetometer (Compass) [part_number="Adafruit #1120"]
  RF_Comms = Adafruit RFM69HCW Transceiver Radio [part_number="Adafruit #3070 and #3071"]
  Part1 = Arduino Mega 2560 (Rev3)
  IC1 = 10-BIT PROGRAMMABLE MAGNETIC ROTARY ENCODER [package=ssop16]
  R1 = Resistor [tolerance=±5% resistance=220 package="0402 [SMD]"]
  Part2 = Soil Moisture Sensor

nets:
  VIN: Pressure.VIN, Part1.3V3
  GND: Pressure.GND, Ambient_Light.GND, DHT1.GND, Compass_+_Accelerometer.GND, RF_Comms.GND, Part1.GND, IC1.VSS
  N1: Pressure.SCK/SCL, Compass_+_Accelerometer.SCL, Part1.D21/SCL
  N2: Pressure.SDI/SDA, Compass_+_Accelerometer.SDA, Part1.D20/SDA
  VIN_2: Pressure.CS, Ambient_Light.VCC, DHT1.VDD, Compass_+_Accelerometer.VIN, RF_Comms.VIN, Part1.5V, IC1.T_B_1, IC1.VDD3V3, IC1.VDD5V, R1.Pin_0
  N3: Ambient_Light.S, Part1.A0
  N4: DHT1.DATA, Part1.D22, R1.Pin_1
  N5: J$1.SIGNAL, RF_Comms.ANTENNA
  N6: RF_Comms.DIO0, Part1.D2_PWM
  N7: RF_Comms.SCK, Part1.D52
  N8: RF_Comms.MISO, Part1.D50
  N9: RF_Comms.MOSI, Part1.D51
  N10: RF_Comms.CS, Part1.D49
  N11: RF_Comms.RST, Part1.D48
  N12: Part1.A1, Part2.SIG
  N13: Part1.D38, IC1.A_LSB_U
  N14: Part1.D39, IC1.B_DIR_V
  N15: Part1.D40, IC1.INDEX_W

notes:
  BMP280 can take 3.3 - 5v. 3Vo can output 3volts (up to 100mA)
  This is just a placeholder for the actual rain sensor which works very much the same way as this moisture sensor.

custom parts:
  Adafruit_BMP280: Bosch has stepped up their game with their new BMP280 sensor, an environmental sensor with temperature, barometric pressure that is the next generation upgrade to the BMP085/BMP180/BMP183. This sensor is great for all sorts of weather sensing and can even be used in both I2C and SPI! This precision sensor from Bosch is the best low-cost, precision sensing solution for measuring barometric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
  Adafruit LSM303DLHC Triple-axis Accelerometer+Magnetometer (Compass): He told you "Go West, young maker!" - but you don't know which way is West! Ah, if only you had this triple-axis accelerometer/magnetometer compass module. Inside are two sensors, one is a classic 3-axis accelerometer, which can tell you which direction is down towards the Earth (by measuring gravity). The other is a magnetometer that can sense where the strongest magnetic force is coming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
  Adafruit RFM69HCW Transceiver Radio: Sending data over long distances is like magic, and now you can be a magician with this range of powerful and easy-to-use radio modules. Sure, sometimes you want to talk to a computer (a good time to use WiFi) or perhaps communicate with a Phone (choose Bluetooth Low Energy!) but what if you want to send data very far? Most WiFi, Bluetooth, Zigbee and other wireless chipsets use 2.4GHz, which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
  10-BIT PROGRAMMABLE MAGNETIC ROTARY ENCODER: 10-BIT PROGRAMMABLE MAGNETIC ROTARY ENCODER Source: www.austriamicrosystems.com .. AS5040DataSheetRev12.pdf
